// Logisim project question1.circ as structural Verilog: 1 circuit, main circuit main
module main (
  input  I3,
  input  I2,
  input  I1,
  input  I0,
  output O1,
  output O0
);

  wire and_1_out, and_2_out, and_3_out, and_4_out, and_5_out, and_6_out, and_7_out, and_8_out, and_9_out,
       not_1_out, not_2_out, not_3_out, not_4_out, not_5_out, not_6_out, not_7_out, not_8_out, not_9_out,
       or_1_out, or_2_out, or_3_out;

  not not_1 (not_1_out, I3);
  and and_1 (and_1_out, not_1_out, not_2_out);
  not not_2 (not_2_out, I2);
  not not_3 (not_3_out, I0);
  and and_2 (and_2_out, not_3_out, I1);
  not not_4 (not_4_out, I3);
  and and_3 (and_3_out, not_4_out, not_5_out);
  not not_5 (not_5_out, I1);
  not not_6 (not_6_out, I0);
  and and_4 (and_4_out, not_6_out, I2);
  not not_7 (not_7_out, I2);
  and and_5 (and_5_out, not_7_out, not_8_out);
  not not_8 (not_8_out, I1);
  not not_9 (not_9_out, I0);
  and and_6 (and_6_out, not_9_out, I3);
  and and_7 (and_7_out, and_1_out, and_2_out);
  and and_8 (and_8_out, and_3_out, and_4_out);
  and and_9 (and_9_out, and_5_out, and_6_out);
  or or_1 (or_1_out, and_8_out, and_9_out);
  buf or_2 (or_2_out, and_7_out);  // OR_Gate
  buf or_3 (or_3_out, and_9_out);  // OR_Gate
  buf or_4 (O1, or_1_out);  // OR_Gate
  or or_5 (O0, or_2_out, or_3_out);
endmodule
