// Logisim project question1.circ as structural Verilog: 1 circuit, main circuit main
module main (
  input  S3,
  input  S2,
  input  S1,
  input  S0,
  input  E,
  output out_6,
  output Y11,
  output Y10,
  output out_9,
  output Y9,
  output Y8,
  output Y7,
  output Y6,
  output Y5,
  output Y4,
  output Y3,
  output Y2,
  output Y1,
  output Y0
);

  wire and_1_out, and_2_out, and_3_out, and_4_out, n2_to_4_decoder_x2_74155_2_p6,
       n2_to_4_decoder_x2_74155_3_p4, not_1_out, not_2_out, not_3_out, not_4_out;

  not not_1 (not_1_out, S2);
  and and_1 (and_1_out, not_1_out, not_2_out);
  not not_2 (not_2_out, S3);
  not not_3 (not_3_out, S3);
  and and_2 (and_2_out, not_3_out, S2);
  not not_4 (not_4_out, S2);
  and and_3 (and_3_out, not_4_out, S3);
  // _2_to_4_Decoder__x2___74155 #(.Facing("east")) 2_to_4_decoder_x2_74155_1: pin names not known; wires that end beside it: S0, S1, Y0, Y1, Y2, Y3
  and and_4 (and_4_out, and_1_out, E);
  // _2_to_4_Decoder__x2___74155 #(.Facing("east")) 2_to_4_decoder_x2_74155_2: pin names not known; wires that end beside it: S0, S1, 1'b0, 1'b0, and_4_out, n2_to_4_decoder_x2_74155_2_p6, 1'b0, 1'b0, 1'b0, 1'b0, Y4, Y5, Y6, Y7
  and and_5 (n2_to_4_decoder_x2_74155_2_p6, and_2_out, E);
  // _2_to_4_Decoder__x2___74155 #(.Facing("east")) 2_to_4_decoder_x2_74155_3: pin names not known; wires that end beside it: S0, S1, 1'b0, n2_to_4_decoder_x2_74155_3_p4, 1'b0, 1'b0, Y8, Y9, out_9, out_6
  and and_6 (n2_to_4_decoder_x2_74155_3_p4, and_3_out, E);

  assign Y10 = out_9;
  assign Y11 = out_6;
endmodule
