// Logisim project question2.circ as structural Verilog: 1 circuit, main circuit main
module main (
  input  I0,
  input  S1,
  input  S0,
  output out_4,
  output O3,
  output O2,
  output out_7,
  output O1,
  output O0
);

  wire not_1_out, not_2_out, not_3_out, not_4_out;

  // _2_to_4_Decoder__x2___74155 #(.Facing("east")) 2_to_4_decoder_x2_74155_1: pin names not known; wires that end beside it: S0, S1, 1'b0, 1'b1, 1'b0, 1'b0
  // NOT_Gate not_1 has open pins: in=open, out=not_1_out
  // NOT_Gate not_2 has open pins: in=open, out=not_2_out
  // NOT_Gate not_3 has open pins: in=open, out=not_3_out
  // NOT_Gate not_4 has open pins: in=open, out=not_4_out
  and and_1 (O3, not_4_out, I0);
  and and_2 (O2, not_3_out, I0);
  and and_3 (O1, not_2_out, I0);
  and and_4 (O0, not_1_out, I0);

  assign out_4 = O3;
  assign out_7 = O2;
endmodule
