// Logisim project e2589877.circ as structural Verilog: 1 circuit, main circuit main
module main (
  input  O3,
  input  O2,
  input  O1,
  input  O0,
  input  A1,
  input  A0,
  input  B1,
  input  B0,
  output L0,
  output L1,
  output L2,
  output L3,
  output L4,
  output L5,
  output L6,
  output L7,
  output L8,
  output L9,
  output S,
  output C,
  output Z,
  output P,
  output E,
  output G,
  output L
);

  wire and_1_out, and_2_out, and_3_out, and_4_out, and_5_out, and_6_out, and_7_out, and_8_out, and_9_out,
       and_10_out, and_11_out, and_12_out, and_13_out, and_14_out, and_15_out, and_16_out, and_17_out,
       and_18_out, and_19_out, and_20_out, and_21_out, and_22_out, and_23_out, and_24_out, and_25_out,
       and_26_out, and_27_out, and_28_out, and_29_out, and_30_out, and_31_out, and_32_out, and_33_out,
       and_34_out, and_35_out, and_36_out, and_37_out, and_38_out, and_39_out, and_40_out, and_41_out,
       and_42_out, and_43_out, and_44_out, and_45_out, and_46_out, and_47_out, and_48_out, and_49_out,
       and_50_out, and_51_out, and_52_out, and_53_out, and_54_out, and_55_out, and_56_out, and_57_out,
       and_58_out, and_59_out, and_60_out, and_61_out, and_62_out, and_63_out, and_64_out, and_65_out,
       and_66_out, and_67_out, and_68_out, and_69_out, and_70_out, and_71_out, and_72_out, and_73_out,
       and_74_out, and_75_out, and_76_out, and_77_out, and_78_out, and_79_out, and_80_out, and_81_out,
       and_82_out, and_83_out, and_84_out, and_85_out, and_86_out, and_87_out, and_88_out, and_89_out,
       and_90_out, and_91_out, and_92_out, and_93_out, and_94_out, and_95_out, and_96_out, and_97_out,
       and_98_out, and_99_out, and_100_out, and_101_out, and_102_out, and_103_out, and_104_out, and_106_out,
       and_107_out, and_108_out, and_109_out, and_110_out, and_111_out, and_112_out, and_114_out,
       and_115_out, and_116_out, and_118_out, and_122_out, and_123_out, and_124_out, and_125_out,
       and_126_out, and_127_out, and_128_out, and_129_out, and_130_out, and_132_out, and_133_out,
       and_134_out, and_135_out, and_136_out, and_137_out, not_1_out, not_2_out, not_3_out, not_4_out,
       not_6_out, not_7_out, not_8_out, not_9_out, not_10_out, not_11_out, not_12_out, not_13_out,
       not_14_out, not_15_out, not_16_out, not_17_out, not_18_out, not_19_out, not_20_out, not_21_out,
       not_22_out, or_1_out, or_2_out, or_3_out, or_4_out, or_5_out, or_6_out, or_7_out, or_8_out, or_9_out,
       or_10_out, or_11_out, or_12_out, or_13_out, or_14_out, or_15_out, or_16_out, or_17_out, or_18_out,
       or_19_out, or_20_out, or_21_out, or_22_out, or_23_out, or_24_out, or_25_out, or_26_out, or_27_out,
       or_28_out, or_29_out, or_30_out, or_31_out, or_32_out, or_33_out, or_34_out, or_35_out, or_36_out,
       or_37_out, or_38_out, or_39_out, or_40_out, or_41_out, or_42_out, or_43_out, or_44_out, or_45_out,
       or_46_out, or_47_out, or_48_out, or_49_out, or_50_out, or_51_out, or_52_out, or_53_out, or_54_out,
       or_55_out, or_56_out, or_57_out, or_58_out, or_59_out, or_60_out, or_61_out, or_62_out, or_63_out,
       or_64_out, or_65_out, or_66_out, or_67_out, or_68_out, or_69_out, or_70_out, or_71_out, or_72_out,
       or_73_out, or_76_out, or_77_out, or_78_out, or_79_out, or_80_out, or_84_out, or_86_out, or_87_out,
       or_88_out;

  not not_1 (not_1_out, A1);
  not not_2 (not_2_out, A0);
  not not_3 (not_3_out, B1);
  not not_4 (not_4_out, B0);
  // _3_to_8_decoder__74138 #(.Facing("east")) 3_to_8_decoder_74138_1: pin names not known; wires that end beside it: O0, O1, O2
  // NOT_Gate not_5 has open pins: in=O3, out=open
  // _3_to_8_decoder__74138 #(.Facing("east")) 3_to_8_decoder_74138_2: pin names not known; wires that end beside it: O2, O1, O0, O3, 1'b0, 1'b0, 1'b0, 1'b0
  // NOT_Gate not_6 has open pins: in=open, out=not_6_out
  // NOT_Gate not_7 has open pins: in=open, out=not_7_out
  // NOT_Gate not_8 has open pins: in=open, out=not_8_out
  // NOT_Gate not_9 has open pins: in=open, out=not_9_out
  // NOT_Gate not_10 has open pins: in=open, out=not_10_out
  // NOT_Gate not_11 has open pins: in=open, out=not_11_out
  // NOT_Gate not_12 has open pins: in=open, out=not_12_out
  // NOT_Gate not_13 has open pins: in=open, out=not_13_out
  // NOT_Gate not_14 has open pins: in=open, out=not_14_out
  and and_1 (and_1_out, not_1_out, not_2_out);
  and and_2 (and_2_out, not_1_out, A0);
  and and_3 (and_3_out, A1, not_2_out);
  and and_4 (and_4_out, A1, A0);
  and and_5 (and_5_out, not_3_out, not_4_out);
  and and_6 (and_6_out, not_3_out, B0);
  and and_7 (and_7_out, B1, not_4_out);
  and and_8 (and_8_out, B1, B0);
  and and_9 (and_9_out, and_2_out, and_8_out);
  and and_10 (and_10_out, and_2_out, and_7_out);
  and and_11 (and_11_out, and_4_out, and_7_out);
  and and_12 (and_12_out, and_3_out, and_8_out);
  and and_13 (and_13_out, and_2_out, and_6_out);
  and and_14 (and_14_out, and_2_out, and_7_out);
  or or_1 (or_1_out, and_14_out, and_15_out);
  and and_15 (and_15_out, and_3_out, and_6_out);
  and and_16 (and_16_out, and_4_out, and_6_out);
  or or_2 (or_2_out, and_16_out, and_17_out);
  and and_17 (and_17_out, and_2_out, and_8_out);
  and and_18 (and_18_out, and_3_out, and_7_out);
  and and_19 (and_19_out, and_4_out, and_7_out);
  or or_3 (or_3_out, and_19_out, and_20_out);
  and and_20 (and_20_out, and_8_out, and_3_out);
  and and_21 (and_21_out, and_8_out, and_4_out);
  and and_22 (and_22_out, and_2_out, and_6_out);
  or or_4 (or_4_out, and_22_out, and_23_out);
  and and_23 (and_23_out, and_3_out, and_7_out);
  or or_5 (or_5_out, or_4_out, or_6_out);
  and and_24 (and_24_out, and_4_out, and_7_out);
  or or_6 (or_6_out, and_24_out, and_25_out);
  and and_25 (and_25_out, and_4_out, and_8_out);
  and and_26 (and_26_out, and_3_out, and_6_out);
  and and_27 (and_27_out, and_4_out, and_6_out);
  and and_28 (and_28_out, and_1_out, and_6_out);
  or or_7 (or_7_out, and_28_out, and_29_out);
  and and_29 (and_29_out, and_2_out, and_5_out);
  and and_30 (and_30_out, and_1_out, and_7_out);
  or or_8 (or_8_out, and_30_out, and_31_out);
  and and_31 (and_31_out, and_5_out, and_3_out);
  or or_9 (or_9_out, or_8_out, and_32_out);
  and and_32 (and_32_out, and_2_out, and_6_out);
  and and_33 (and_33_out, and_1_out, and_8_out);
  or or_10 (or_10_out, and_33_out, and_34_out);
  and and_34 (and_34_out, and_5_out, and_4_out);
  or or_11 (or_11_out, or_10_out, or_12_out);
  and and_35 (and_35_out, and_2_out, and_7_out);
  or or_12 (or_12_out, and_35_out, and_36_out);
  and and_36 (and_36_out, and_6_out, and_3_out);
  and and_37 (and_37_out, and_4_out, and_6_out);
  or or_13 (or_13_out, and_37_out, and_38_out);
  and and_38 (and_38_out, and_2_out, and_8_out);
  or or_14 (or_14_out, or_13_out, and_39_out);
  and and_39 (and_39_out, and_7_out, and_3_out);
  and and_40 (and_40_out, and_3_out, and_8_out);
  or or_15 (or_15_out, and_40_out, and_41_out);
  and and_41 (and_41_out, and_7_out, and_4_out);
  and and_42 (and_42_out, and_4_out, and_8_out);
  and and_43 (and_43_out, and_1_out, and_6_out);
  or or_16 (or_16_out, and_43_out, and_44_out);
  and and_44 (and_44_out, and_2_out, and_7_out);
  or or_17 (or_17_out, or_16_out, and_45_out);
  and and_45 (and_45_out, and_3_out, and_8_out);
  or or_18 (or_18_out, or_17_out, or_19_out);
  and and_46 (and_46_out, and_2_out, and_5_out);
  or or_19 (or_19_out, and_46_out, or_20_out);
  and and_47 (and_47_out, and_3_out, and_6_out);
  or or_20 (or_20_out, and_47_out, and_48_out);
  and and_48 (and_48_out, and_4_out, and_7_out);
  and and_49 (and_49_out, and_1_out, and_7_out);
  or or_21 (or_21_out, and_49_out, and_50_out);
  and and_50 (and_50_out, and_2_out, and_8_out);
  or or_22 (or_22_out, or_21_out, or_23_out);
  and and_51 (and_51_out, and_3_out, and_5_out);
  or or_23 (or_23_out, and_51_out, and_52_out);
  and and_52 (and_52_out, and_4_out, and_6_out);
  and and_53 (and_53_out, and_1_out, and_8_out);
  or or_24 (or_24_out, and_53_out, and_54_out);
  and and_54 (and_54_out, and_8_out, and_1_out);
  and and_55 (and_55_out, and_2_out, and_5_out);
  or or_25 (or_25_out, and_55_out, and_56_out);
  and and_56 (and_56_out, and_3_out, and_5_out);
  or or_26 (or_26_out, or_25_out, and_57_out);
  and and_57 (and_57_out, and_3_out, and_6_out);
  or or_27 (or_27_out, or_26_out, or_28_out);
  and and_58 (and_58_out, and_4_out, and_5_out);
  or or_28 (or_28_out, and_58_out, or_29_out);
  and and_59 (and_59_out, and_4_out, and_6_out);
  or or_29 (or_29_out, and_59_out, and_60_out);
  and and_60 (and_60_out, and_4_out, and_7_out);
  and and_61 (and_61_out, and_6_out, and_1_out);
  or or_30 (or_30_out, and_61_out, and_62_out);
  and and_62 (and_62_out, and_7_out, and_1_out);
  or or_31 (or_31_out, or_30_out, and_63_out);
  and and_63 (and_63_out, and_7_out, and_2_out);
  or or_32 (or_32_out, or_31_out, or_33_out);
  and and_64 (and_64_out, and_8_out, and_1_out);
  or or_33 (or_33_out, and_64_out, or_34_out);
  and and_65 (and_65_out, and_8_out, and_2_out);
  or or_34 (or_34_out, and_65_out, and_66_out);
  and and_66 (and_66_out, and_8_out, and_3_out);
  and and_67 (and_67_out, and_1_out, and_5_out);
  or or_35 (or_35_out, and_67_out, and_68_out);
  and and_68 (and_68_out, and_2_out, and_6_out);
  or or_36 (or_36_out, or_35_out, or_37_out);
  and and_69 (and_69_out, and_3_out, and_7_out);
  or or_37 (or_37_out, and_69_out, and_70_out);
  and and_70 (and_70_out, and_4_out, and_8_out);
  and and_71 (and_71_out, and_6_out, and_2_out);
  or or_38 (or_38_out, and_71_out, and_72_out);
  and and_72 (and_72_out, and_2_out, and_8_out);
  or or_39 (or_39_out, or_38_out, and_73_out);
  and and_73 (and_73_out, and_4_out, and_6_out);
  and and_74 (and_74_out, and_7_out, and_3_out);
  or or_40 (or_40_out, and_74_out, and_75_out);
  and and_75 (and_75_out, and_4_out, and_7_out);
  or or_41 (or_41_out, or_40_out, and_76_out);
  and and_76 (and_76_out, and_3_out, and_8_out);
  and and_77 (and_77_out, and_8_out, and_4_out);
  and and_78 (and_78_out, and_2_out, and_5_out);
  or or_42 (or_42_out, and_78_out, and_79_out);
  and and_79 (and_79_out, and_1_out, and_6_out);
  or or_43 (or_43_out, or_42_out, and_80_out);
  and and_80 (and_80_out, and_2_out, and_6_out);
  and and_81 (and_81_out, and_1_out, and_7_out);
  or or_44 (or_44_out, and_81_out, and_82_out);
  and and_82 (and_82_out, and_5_out, and_3_out);
  or or_45 (or_45_out, or_44_out, and_83_out);
  and and_83 (and_83_out, and_3_out, and_7_out);
  or or_46 (or_46_out, and_4_out, and_8_out);
  or or_47 (or_47_out, or_46_out, and_84_out);
  and and_84 (and_84_out, and_3_out, and_6_out);
  or or_48 (or_48_out, or_47_out, and_85_out);
  and and_85 (and_85_out, and_2_out, and_7_out);
  and and_86 (and_86_out, and_1_out, and_6_out);
  or or_49 (or_49_out, and_86_out, and_87_out);
  and and_87 (and_87_out, and_2_out, and_5_out);
  or or_50 (or_50_out, or_49_out, or_51_out);
  and and_88 (and_88_out, and_8_out, and_3_out);
  or or_51 (or_51_out, and_88_out, and_89_out);
  and and_89 (and_89_out, and_4_out, and_7_out);
  and and_90 (and_90_out, and_1_out, and_7_out);
  or or_52 (or_52_out, and_90_out, and_91_out);
  and and_91 (and_91_out, and_3_out, and_5_out);
  or or_53 (or_53_out, or_52_out, or_54_out);
  and and_92 (and_92_out, and_2_out, and_8_out);
  or or_54 (or_54_out, and_92_out, and_93_out);
  and and_93 (and_93_out, and_6_out, and_4_out);
  and and_94 (and_94_out, and_1_out, and_8_out);
  or or_55 (or_55_out, and_94_out, and_95_out);
  and and_95 (and_95_out, and_5_out, and_4_out);
  or or_56 (or_56_out, or_55_out, or_57_out);
  and and_96 (and_96_out, and_2_out, and_7_out);
  or or_57 (or_57_out, and_96_out, and_97_out);
  and and_97 (and_97_out, and_6_out, and_3_out);
  or or_58 (or_58_out, and_9_out, and_10_out);
  or or_59 (or_59_out, or_58_out, and_11_out);
  and and_98 (and_98_out, or_59_out, not_6_out);
  and and_99 (and_99_out, and_12_out, not_6_out);
  and and_100 (and_100_out, and_13_out, not_7_out);
  and and_101 (and_101_out, or_1_out, not_7_out);
  and and_102 (and_102_out, or_2_out, not_7_out);
  and and_103 (and_103_out, and_18_out, not_7_out);
  and and_104 (and_104_out, or_3_out, not_7_out);
  and and_105 (L9, and_21_out, not_7_out);
  and and_106 (and_106_out, or_5_out, not_8_out);
  and and_107 (and_107_out, and_26_out, not_8_out);
  and and_108 (and_108_out, and_27_out, not_8_out);
  and and_109 (and_109_out, or_7_out, not_9_out);
  and and_110 (and_110_out, or_9_out, not_9_out);
  and and_111 (and_111_out, or_11_out, not_9_out);
  and and_112 (and_112_out, or_14_out, not_9_out);
  and and_113 (L5, or_15_out, not_9_out);
  and and_114 (and_114_out, and_42_out, not_9_out);
  and and_115 (and_115_out, or_18_out, not_10_out);
  or or_60 (or_60_out, or_17_out, or_21_out);
  and and_116 (and_116_out, or_22_out, not_10_out);
  or or_61 (or_61_out, or_60_out, and_53_out);
  and and_117 (S, or_61_out, not_10_out);
  and and_118 (and_118_out, or_24_out, not_10_out);
  and and_119 (G, or_27_out, not_11_out);
  and and_120 (L, or_32_out, not_11_out);
  and and_121 (E, or_36_out, not_11_out);
  and and_122 (and_122_out, or_39_out, not_12_out);
  and and_123 (and_123_out, or_41_out, not_12_out);
  and and_124 (and_124_out, and_77_out, not_12_out);
  and and_125 (and_125_out, or_43_out, not_13_out);
  and and_126 (and_126_out, or_45_out, not_13_out);
  and and_127 (and_127_out, or_48_out, not_13_out);
  and and_128 (and_128_out, or_50_out, not_14_out);
  and and_129 (and_129_out, or_53_out, not_14_out);
  and and_130 (and_130_out, or_56_out, not_14_out);
  or or_62 (or_62_out, and_98_out, and_100_out);
  or or_63 (or_63_out, and_99_out, and_101_out);
  or or_64 (or_64_out, or_62_out, and_106_out);
  or or_65 (or_65_out, or_64_out, and_109_out);
  or or_66 (or_66_out, or_67_out, and_110_out);
  or or_67 (or_67_out, or_63_out, and_107_out);
  or or_68 (or_68_out, and_102_out, and_108_out);
  or or_69 (or_69_out, or_70_out, and_122_out);
  or or_70 (or_70_out, or_65_out, and_115_out);
  or or_71 (or_71_out, or_66_out, and_116_out);
  or or_72 (or_72_out, or_68_out, and_111_out);
  or or_73 (or_73_out, or_72_out, and_118_out);
  or or_74 (L4, and_103_out, and_112_out);
  or or_75 (L6, and_104_out, and_114_out);
  or or_76 (or_76_out, or_69_out, and_125_out);
  or or_77 (or_77_out, or_78_out, and_126_out);
  or or_78 (or_78_out, or_71_out, and_123_out);
  or or_79 (or_79_out, or_80_out, and_127_out);
  or or_80 (or_80_out, or_73_out, and_124_out);
  or or_81 (L1, or_76_out, and_128_out);
  or or_82 (L2, or_77_out, and_129_out);
  or or_83 (L3, or_79_out, and_130_out);
  not not_15 (not_15_out, L6);
  not not_16 (not_16_out, L5);
  not not_17 (not_17_out, L1);
  not not_18 (not_18_out, L4);
  not not_19 (not_19_out, L2);
  not not_20 (not_20_out, L3);
  not not_21 (not_21_out, L9);
  or or_84 (or_84_out, L1, L2);
  or or_85 (P, or_84_out, L4);
  or or_86 (or_86_out, L4, L5);
  or or_87 (or_87_out, or_86_out, or_88_out);
  and and_131 (C, or_87_out, not_9_out);
  or or_88 (or_88_out, L6, L9);
  and and_132 (and_132_out, not_18_out, not_16_out);
  and and_133 (and_133_out, and_132_out, and_134_out);
  and and_134 (and_134_out, not_15_out, not_21_out);
  and and_135 (and_135_out, and_133_out, not_17_out);
  and and_136 (and_136_out, and_135_out, and_137_out);
  and and_137 (and_137_out, not_20_out, not_19_out);
  and and_138 (L0, and_136_out, not_22_out);
  not not_22 (not_22_out, not_11_out);

  assign L7 = 1'b0;
  assign L8 = 1'b0;
  assign Z = L0;

  // Notes on the sheet:
  //   OPCODE 1 (A%B)
  //   OPCODE 2 (A*B)
  //   OPCODE 3 (A/B)
  //   OPCODE 4 (A+B)
  //   OPCODE 5 (A-B)
  //   OPCODE 6 (Comparison)
  //   OPCODE 7 (Bitwise AND)
  //   OPCODE 8 (Bitwise OR)
  //   OPCODE 9 (Bitwise XOR)
  //   PARITY CASE
  //   CARRY CASE
  //   0 CASE
endmodule
